# Fritzing sketch baby_mobile (saved by Fritzing 0.8.7b)
breadboards: 1

parts:
  Part1 = Arduino Uno (Rev3)
  Part2 = 2A MOTOR SHIELD AMPERKA
  IR1 = TSOP22 [package=THT]
  SP1 = SPEAKER [package=pcb_mount_speaker]
  MP1 = DFPlayerMini [chip_label=IC package="DIP (Dual Inline) [THT]"]
  C1 = Capacitor [package=cap-pth-small2]
  R1 = Resistor [tolerance=±5% resistance=220 package=THT]
  R2 = Resistor [tolerance=±5% resistance=220 package=THT]
  M1 = DC Motor
  R3 = Resistor [tolerance=±5% resistance=220 package=THT]
  LED5 = RGB LED (com. cathode, rgb) [package="5 mm [THT]"]
  R4 = Resistor [tolerance=±5% resistance=220 package=THT]
  R5 = Resistor [tolerance=±5% resistance=220 package=THT]

nets:
  N1: Part1.A0, Part2.A0
  N2: Part1.A1, Part2.A1
  N3: Part1.A2, Part2.A2
  N4: Part1.A3, Part2.A3
  N5: Part1.A4/SDA, Part2.A4
  N6: Part1.A5/SCL, Part2.A5
  N7: Part1.D8, Part2.D8
  N8: Part1.D9_PWM, Part2.D9, R4.Pin_1
  N9: Part1.D10_PWM/SS, Part2.D10, R5.Pin_1
  N10: Part1.D11_PWM/MOSI, Part2.D11
  N11: Part1.D12/MISO, Part2.D12, R1.Pin_1
  N12: Part1.D13/SCK, Part2.D13, R2.Pin_1
  GND: Part1.GND, Part2.GND, IR1.GND, IR1.Vs, MP1.GND#6, LED5.common_cathode
  N13: Part1.AREF, Part2.AREF
  N14: Part1.D0/RX, Part2.D0
  N15: Part1.D1/TX, Part2.D1
  N16: Part1.D2, Part2.D2, IR1.OUT
  N17: Part1.D3_PWM, Part2.D3, MP1.Busy
  N18: Part1.D4, Part2.D4
  N19: Part1.D5_PWM, Part2.D5
  N20: Part1.D6_PWM, Part2.D6, R3.Pin_1
  N21: Part1.D7, Part2.D7
  N22: Part1.RESET, Part2.RST
  3V3: Part1.3V3, Part2.3V3
  5V: Part1.5V, Part2.5V, MP1.VCC
  VIN: Part1.VIN, Part2.VIN
  N23: Part2.M1+, C1.2, M1.pin_1
  N24: Part2.M1-, C1.1, M1.pin_2
  N25: SP1.+, MP1.SPK_2
  N26: SP1.-, MP1.SPK_1
  N27: MP1.RX, R1.Pin_0
  N28: MP1.TX, R2.Pin_0
  N29: R3.Pin_0, LED5.blue_anode
  N30: LED5.red_anode, R5.Pin_0
  N31: LED5.green_anode, R4.Pin_0

custom parts:
  TSOP22: The TSOP22.. - series are miniaturized receivers for infrared remote control systems. PIN diode and preamplifier are assembled on lead frame, the epoxy package is designed as IR filter. The demodulated output signal can directly be decoded by a microprocessor. TSOP22.. is the standard IR remote control receiver series, supporting all major transmission codes.
  DFPlayerMini: DFPLayer Mini module is a serial MP3 module provides the perfect integrated MP3, WMV hardware decoding. While the software supports TF card driver, supports FAT16, FAT32 file system. Through simple serial commands to specify music playing, as well as how t o play music and other functions, without the cumbersome underlying operating, easy to use, stable and reliable are the most important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
